# Fritzing sketch Gavin_DPV_Core (saved by Fritzing 0.9.3b)
circuit board: 9.4687cm x 9.01911cm
breadboards: 1

parts:
  Part2 = Adafruit PCF8523 RTC [part_number="Adafruit #3295"]
  Part4 = Adafruit BME280
  Part5 = Adafruit 4-channel I2C-safe Bi-directional Logic Level Converter [part_number="Adafruit #757"]
  Part6 = Adafruit ADS1115 16Bit I2C ADC [part_number="Adafruit #1085"]
  CURRENT_SENSOR1 = CURRENT SENSOR ACS758
  JP1 = Header 5x2 [package=2x5-ra]
  JP2 = Header 5x2 [package=2x5-ra]
  S1 = Pushbutton [package="[THT]"]
  C1 = Capacitor [package=cap-pth-small]
  C2 = Capacitor [package=cap-pth-small]
  R1 = Resistor [tolerance=±5% resistance=220 package=THT]
  MCU1 = Raspberry Pi Zero

nets:
  N1: Part2.SCL, Part4.SCK/SCL, Part5.A1, JP1.4, JP2.8, MCU1.pin_3
  N2: Part2.SDA, Part4.SDI/SDA, Part5.A2, JP1.3, JP2.7, MCU1.pin_5
  VCC: Part2.VCC, Part4.VIN, Part5.LV, JP1.6, MCU1.pin_1, MCU1.pin_17
  GND: Part2.GND, Part4.GND, Part5.GND, Part6.GND, CURRENT_SENSOR1.GND, JP1.5, JP2.2, JP2.4, JP2.6, S1.Pin_1, S1.Pin_2, C1.2, C2.1, MCU1.pin_6, MCU1.pin_14, MCU1.pin_20, MCU1.pin_34, MCU1.pin_39
  N3: Part5.B2, Part6.SCL
  N4: Part5.B1, Part6.SDA
  VDD: Part5.HV, Part6.AIN0, Part6.VDD, CURRENT_SENSOR1.VCC, C1.1, MCU1.pin_2, MCU1.pin_4
  N5: Part6.AIN3, C2.2, R1.Pin_1
  N6: Part6.AIN2, JP2.1
  N7: Part6.AIN1, JP2.3
  N8: CURRENT_SENSOR1.VIOUT, R1.Pin_0
  N9: JP1.7, MCU1.pin_16
  N10: JP1.8, MCU1.pin_12
  N11: JP1.9, MCU1.pin_8
  N12: JP1.10, MCU1.pin_10
  N13: S1.Pin_3, S1.Pin_4, MCU1.pin_7

custom parts:
  Adafruit PCF8523 RTC: This is a great battery-backed real time clock (RTC) that allows your microcontroller project to keep track of time even if it is reprogrammed, or if the power is lost. Perfect for datalogging, clock-building, time stamping, timers and alarms, etc. Equipped with PCF8523 RTC - it can run from 3.3V or 5V power & logic! Works great with an Arduino using our RTC library, with CircuitPython or with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
  Adafruit BME280: Bosch has stepped up their game with their new BME280 sensor, an environmental sensor with temperature, barometric pressure and humidity! This sensor is great for all sorts of weather/environmental sensing and can even be used in both I2C and SPI! This precision sensor from Bosch is the best low-cost sensing solution for measuring humidity with ±3% accuracy, barometric pressure with ±1 hPa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
  Adafruit 4-channel I2C-safe Bi-directional Logic Level Converter: Because the Arduino (and Basic Stamp) are 5V devices, and most modern sensors, displays, flash cards and modes are 3.3V-only, many makers find that they need to perform level shifting/conversion to protect the 3.3V device from 5V. We do have some other handy level shifters in the shop, from the DIP 74LVC245 to the fancy bi-directional TXB0108. However, neither of these are happy to work with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
  Adafruit ADS1115 16Bit I2C ADC: For microcontrollers without an analog-to-digital converter or when you want a higher-precision ADC, the ADS1115 provides 16-bit precision at 860 samples/second over I2C. The chip can be configured as 4 single-ended input channels, or two differential channels. As a nice bonus, it even includes a programmable gain amplifier, up to x16, to help boost up smaller single/differential signals to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
  CURRENT SENSOR ACS758: CURRENT SENSOR
